// Logisim project and4bit.circ as structural Verilog: 1 circuit, main circuit and4bit
module and4bit (
  input  [3:0] a,
  input  [3:0] b,
  output [3:0] y
);

  assign y = a & b;  // AND_Gate and_1, 4 bits wide
endmodule
