// Logisim project full_adder.circ as structural Verilog: 1 circuit, main circuit full_adder
module full_adder (
  input  a,
  input  b,
  input  cin,
  output cout,
  output sum
);

  wire and_1_out, and_2_out, xor_1_out;

  and and_1 (and_1_out, a, b);
  xor xor_1 (xor_1_out, a, b);
  and and_2 (and_2_out, xor_1_out, cin);
  xor xor_2 (sum, xor_1_out, cin);
  or or_1 (cout, and_1_out, and_2_out);
endmodule
