// Logisim project half_adder.circ as structural Verilog: 1 circuit, main circuit half_adder
module half_adder (
  input  a,
  input  b,
  output sum,
  output carry
);

  xor xor_1 (sum, a, b);
  and and_1 (carry, a, b);
endmodule
