// Logisim project xnor3.circ as structural Verilog: 1 circuit, main circuit xnor3
module xnor3 (
  input  a,
  input  b,
  input  c,
  output y
);

  wire xor_1_out;

  ExactlyOne xor_1 (.out(xor_1_out), .in0(a), .in1(b), .in2(c));
  not not_1 (y, xor_1_out);
endmodule
